// Logisim project aiALU.circ as structural Verilog
module aiArith (
  input  [7:0] a,
  input  [7:0] b,
  input  AS,
  input  Cin,
  output [7:0] y
);

  _8bit_Adder u_8bit_adder_1 ();  // open: in_15, in_16, in_14, in_13, in_12, in_11, in_10, in_9, in_8, in_7, in_6, in_5, in_4, in_3, in_2, in_1, in_17, out_18, out_19, out_20, out_21, out_22, out_23, out_24, out_25, out_26
endmodule

module HalfAdder (
  input  A,
  input  B,
  output S,
  output C
);

  xor xor_1 (S, A, B);
  and and_1 (C, A, B);
endmodule

module FullAdder (
  input  A,
  input  B,
  input  Cin,
  output Cout,
  output S
);

  wire halfadder_1_c, halfadder_2_c, halfadder_2_s;

  or or_1 (Cout, halfadder_2_c, halfadder_1_c);
  HalfAdder halfadder_1 (.A(halfadder_2_s), .B(Cin), .S(S), .C(halfadder_1_c));
  HalfAdder halfadder_2 (.A(A), .B(B), .S(halfadder_2_s), .C(halfadder_2_c));
endmodule

module _8bit_Adder (
  input  in_1,
  input  in_2,
  input  in_3,
  input  in_4,
  input  in_5,
  input  in_6,
  input  in_7,
  input  in_8,
  input  in_9,
  input  in_10,
  input  in_11,
  input  in_12,
  input  in_13,
  input  in_14,
  input  in_15,
  input  in_16,
  input  in_17,
  output out_18,
  output out_19,
  output out_20,
  output out_21,
  output out_22,
  output out_23,
  output out_24,
  output out_25,
  output out_26
);

  wire fulladder_2_cout, fulladder_3_cout, fulladder_4_cout, fulladder_5_cout, fulladder_6_cout,
       fulladder_7_cout, fulladder_8_cout;

  FullAdder fulladder_1 (.A(in_2), .B(in_1), .Cin(fulladder_2_cout), .S(out_19), .Cout(out_18));
  FullAdder fulladder_2 (.A(in_4), .B(in_3), .Cin(fulladder_3_cout), .S(out_20), .Cout(fulladder_2_cout));
  FullAdder fulladder_3 (.A(in_6), .B(in_5), .Cin(fulladder_4_cout), .S(out_21), .Cout(fulladder_3_cout));
  FullAdder fulladder_4 (.A(in_8), .B(in_7), .Cin(fulladder_5_cout), .S(out_22), .Cout(fulladder_4_cout));
  FullAdder fulladder_5 (.A(in_10), .B(in_9), .Cin(fulladder_6_cout), .S(out_23), .Cout(fulladder_5_cout));
  FullAdder fulladder_6 (.A(in_12), .B(in_11), .Cin(fulladder_7_cout), .S(out_24), .Cout(fulladder_6_cout));
  FullAdder fulladder_7 (.A(in_14), .B(in_13), .Cin(fulladder_8_cout), .S(out_25), .Cout(fulladder_7_cout));
  FullAdder fulladder_8 (.A(in_16), .B(in_15), .Cin(in_17), .S(out_26), .Cout(fulladder_8_cout));
endmodule

module Sommatore_Sottrattore_8bit (
  input  [7:0] in_1,
  input  in_2,
  input  [7:0] in_3,
  input  in_4
);

  wire n8bit_adder_2_out_18, n8bit_adder_2_out_19, n8bit_adder_2_out_20, n8bit_adder_2_out_21,
       n8bit_adder_2_out_22, n8bit_adder_2_out_23, n8bit_adder_2_out_24, n8bit_adder_2_out_25,
       n8bit_adder_2_out_26, not_1_out, not_2_out, not_3_out, not_4_out, not_5_out, not_6_out, not_7_out,
       not_8_out;

  not not_1 (not_1_out, in_1[5]);
  not not_2 (not_2_out, in_1[6]);
  not not_3 (not_3_out, in_1[7]);
  _8bit_Adder u_8bit_adder_1 (
    .in_15(n8bit_adder_2_out_26), .in_16(in_3[0]), .in_14(n8bit_adder_2_out_25), .in_13(in_3[1]),
    .in_12(n8bit_adder_2_out_24), .in_11(in_3[2]), .in_10(n8bit_adder_2_out_23), .in_9(in_3[3]),
    .in_8(n8bit_adder_2_out_22), .in_7(in_3[4]), .in_6(n8bit_adder_2_out_21), .in_5(in_3[5]),
    .in_4(n8bit_adder_2_out_20), .in_3(in_3[6]), .in_2(n8bit_adder_2_out_19), .in_1(in_3[7]), .in_17(in_4));  // open: out_18, out_19, out_20, out_21, out_22, out_23, out_24, out_25, out_26
  not not_4 (not_4_out, in_1[3]);
  not not_5 (not_5_out, in_1[4]);
  not not_6 (not_6_out, in_1[1]);
  not not_7 (not_7_out, in_1[0]);
  not not_8 (not_8_out, in_1[2]);
  _8bit_Adder u_8bit_adder_2 (
    .in_15(not_7_out), .in_16(1'b1), .in_14(not_6_out), .in_13(1'b0), .in_12(not_8_out), .in_11(1'b0),
    .in_10(not_4_out), .in_9(1'b0), .in_8(not_5_out), .in_7(1'b0), .in_6(not_1_out), .in_5(1'b0),
    .in_4(not_2_out), .in_3(1'b0), .in_2(not_3_out), .in_1(1'b0), .in_17(in_2),
    .out_18(n8bit_adder_2_out_18), .out_19(n8bit_adder_2_out_19), .out_20(n8bit_adder_2_out_20),
    .out_21(n8bit_adder_2_out_21), .out_22(n8bit_adder_2_out_22), .out_23(n8bit_adder_2_out_23),
    .out_24(n8bit_adder_2_out_24), .out_25(n8bit_adder_2_out_25), .out_26(n8bit_adder_2_out_26));
endmodule
